# Fritzing sketch Smart Moneybag (saved by Fritzing 0.8.7b)

parts:
  CNY70-2 = CNY70 [package=cny70-side]
  Q2 = NPN-Transistor [package="TO92 [THT]"]
  R5 = Resistor [tolerance=±5% resistance=100 package=THT]
  R6 = Resistor [tolerance=±5% resistance=10k package=THT]
  Arduino_Pro_Mini1 = Arduino Pro Mini v13
  R7 = Resistor [tolerance=±5% resistance=1k package=THT]
  S3 = Pushbutton [package="[THT]"]
  J2 = Piezo Speaker
  Q3 = NPN-Transistor [package="TO92 [THT]"]
  R8 = Resistor [tolerance=±5% resistance=1k package=THT]
  LED2 = LED - 5mm [color="Red (633nm)" package="5 mm [THT]"]

nets:
  N1: CNY70-2.A, R5.Pin_0
  N2: CNY70-2.C, Q2.E, Arduino_Pro_Mini1.GND, S3.Pin_3, S3.Pin_4, Q3.E, LED2.cathode
  N3: CNY70-2.E, R6.Pin_1, Arduino_Pro_Mini1.A0
  N4: CNY70-2.K, Q2.C
  N5: Q2.B, R7.Pin_1
  N6: R5.Pin_1, R6.Pin_0, Arduino_Pro_Mini1.VCC, J2.pin2
  N7: Arduino_Pro_Mini1.A1, R7.Pin_0
  N8: Arduino_Pro_Mini1.D13/SCK, LED2.anode
  N9: Arduino_Pro_Mini1.D6_PWM, R8.Pin_1
  N10: Arduino_Pro_Mini1.D2, S3.Pin_1
  N11: J2.pin1, Q3.C
  N12: Q3.B, R8.Pin_0

custom parts:
  CNY70: PHOTOTRANSISTOR
