# Fritzing sketch Vertical Parking System Project (saved by Fritzing 0.8.7b)
circuit board: 8.25512cm x 11.562cm

parts:
  Part1 = Arduino Uno (Rev3)
  S1 = Round Pushbutton
  Part2 = Jtron 1 Channel Optoisolated Relay Module [package=relay]
  LCD1 = LCD screen
  LCM1602_IIC1 = LCM1602 IIC [part_number="LCM1602 IIC" chip_label="LCM1602 IIC" package="DIP (Dual Inline) [THT]"]
  M1 = DC Motor
  M2 = E18-D80NK_1 [package=THT]
  M3 = E18-D80NK_1 [package=THT]
  M4 = E18-D80NK_1 [package=THT]
  Part3 = RFID-RC522-v2

nets:
  N1: Part1.A0, M2.pin3
  N2: Part1.A1, M3.pin3
  N3: Part1.A2, M4.pin3
  N4: Part1.A3, S1.leg0
  N5: Part1.A4/SDA, LCM1602_IIC1.SDA
  N6: Part1.A5/SCL, LCM1602_IIC1.SCL
  N7: Part1.D9_PWM, Part3.RST
  N8: Part1.D10_PWM/SS, Part3.SDA
  N9: Part1.D11_PWM/MOSI, Part3.MOSI
  N10: Part1.D12/MISO, Part3.MISO
  N11: Part1.D13/SCK, Part3.SCK
  GND: Part1.GND, S1.leg1, Part2.NO, Part2.GND, LCM1602_IIC1.GND, Part3.GND
  N12: Part1.D2, Part2.IN1
  3V3: Part1.3V3, Part3.3.3V
  VCC: Part1.5V, Part2.VCC, LCM1602_IIC1.VCC, M2.pin2, M3.pin2, M4.pin2
  N13: Part2.NC, M1.pin_1
  N14: Part2.MAIN, M1.pin_2
  VSS: LCD1.VSS, LCM1602_IIC1.VSS
  VDD: LCD1.VDD, LCM1602_IIC1.VDD
  N15: LCD1.V0, LCM1602_IIC1.V0
  N16: LCD1.RS, LCM1602_IIC1.RS
  N17: LCD1.R/W, LCM1602_IIC1.RW
  N18: LCD1.E, LCM1602_IIC1.E
  N19: LCD1.DB0, LCM1602_IIC1.D0
  N20: LCD1.DB1, LCM1602_IIC1.D1
  N21: LCD1.DB2, LCM1602_IIC1.D2
  N22: LCD1.DB3, LCM1602_IIC1.D3
  N23: LCD1.DB4, LCM1602_IIC1.D4
  N24: LCD1.DB5, LCM1602_IIC1.D5
  N25: LCD1.DB6, LCM1602_IIC1.D6
  N26: LCD1.DB7, LCM1602_IIC1.D7
  N27: LCD1.LED-, LCM1602_IIC1.A
  N28: LCD1.LED+, LCM1602_IIC1.K
  N29: M2.pin1, M3.pin1, M4.pin1

custom parts:
  LCD screen: A standard character display, usually with 2x16 characters. Comes in many colors.
  LCM1602 IIC: I2C-Module to use a 1602 or 2004 LCD on with the wire.h libory Serial LCD Modul
  E18-D80NK_1: E18-D80NK Proximity Sensor module.
  RFID-RC522-v2: A simple China made RFID-RC522 Reader; do check the pin labels, as this is a MFRC522 based clone.
